# Fritzing sketch CaravanPi-GesamtSchaltplan-V2 (saved by Fritzing 0.9.4)
breadboards: 1

parts:
  Raspberry_Pi_3 = Raspberry Pi 3 [part_number=RPI-3-V1.2]
  PullUp = Resistor [tolerance=±5% resistance=47k package=THT]
  D1 = Rectifier Diode [part_number=1N4003 package="300 mil [THT]"]
  S1 = Pushbutton [part_number="Ein-/Aus Taster" package="[THT]"]
  RCWL-0516_Microwave_Radar_Motion_Sensor1 = RCWL-0516 Microwave Radar Motion Sensor Module
  S2 = Pushbutton [package="[THT]"]
  S3 = Pushbutton [package="[THT]"]
  S4 = Pushbutton [package="[THT]"]
  S5 = Pushbutton [package="[THT]"]
  R2 = Resistor [tolerance=±5% resistance=100k package=THT]
  alle_PullDown's = Resistor [tolerance=±5% resistance=47k package=THT]
  R4 = Resistor [tolerance=±5% resistance=100k package=THT]
  R5 = Resistor [tolerance=±5% resistance=100k package=THT]
  J1 = Piezo Speaker
  LED1 = LEDs [package=led10mm]
  LED2 = LEDs [package=led10mm]
  abhängig_von_LED = Resistor [tolerance=±5% resistance=100 package=THT]
  DS1 = DS18B20 1-Wire Temperature Sensor [part_number=DS18B20]
  DS2 = DS18B20 1-Wire Temperature Sensor [part_number=DS18B20]
  DS3 = DS18B20 1-Wire Temperature Sensor [part_number=DS18B20]
  Bauteil1 = HX711 Weighing Sensor Module
  Bauteil2 = BME280 Breakout
  Bauteil3 = BME280 Breakout
  Bauteil4 = Adafruit ADXL345 [part_number="Adafruit #1231"]
  MCP1 = CJMCU2317-MCP23017
  MCP2 = CJMCU2317-MCP23017
  LED3 = RGB LED (com. cathode, rbg) [package="5 mm [THT]"]
  LED4 = RGB LED (com. cathode, rbg) [package="5 mm [THT]"]
  LED5 = RGB LED (com. cathode, rbg) [package="5 mm [THT]"]
  LED6 = RGB LED (com. cathode, rbg) [package="5 mm [THT]"]
  LED7 = RGB LED (com. cathode, rbg) [package="5 mm [THT]"]
  LED8 = RGB LED (com. cathode, rbg) [package="5 mm [THT]"]
  LED9 = RGB LED (com. cathode, rbg) [package="5 mm [THT]"]
  R7 = Resistor [tolerance=±5% resistance=220 package=THT]
  R8 = Resistor [tolerance=±5% resistance=220 package=THT]
  R9 = Resistor [tolerance=±5% resistance=220 package=THT]
  R10 = Resistor [tolerance=±5% resistance=220 package=THT]
  R11 = Resistor [tolerance=±5% resistance=220 package=THT]
  R12 = Resistor [tolerance=±5% resistance=220 package=THT]
  R13 = Resistor [tolerance=±5% resistance=220 package=THT]
  R14 = Resistor [tolerance=±5% resistance=220 package=THT]
  Alle_Vorwiderstände_abhängig_von_LEDs = Resistor [tolerance=±5% resistance=100 package=THT]
  R16 = Resistor [tolerance=±5% resistance=220 package=THT]
  R17 = Resistor [tolerance=±5% resistance=220 package=THT]
  R18 = Resistor [tolerance=±5% resistance=220 package=THT]
  Alle_Vorwiderstände_abhängig_von_LEDs_2 = Resistor [tolerance=±5% resistance=100 package=THT]
  R20 = Resistor [tolerance=±5% resistance=220 package=THT]
  R21 = Resistor [tolerance=±5% resistance=220 package=THT]
  R22 = Resistor [tolerance=±5% resistance=220 package=THT]
  R23 = Resistor [tolerance=±5% resistance=220 package=THT]
  R24 = Resistor [tolerance=±5% resistance=220 package=THT]
  R25 = Resistor [tolerance=±5% resistance=220 package=THT]
  R26 = Resistor [tolerance=±5% resistance=220 package=THT]
  R27 = Resistor [tolerance=±5% resistance=220 package=THT]
  IC2 = IC, DIP package, 8 pins [chip_label="Horter&Kalb I2C Externder"]
  IC3 = IC, DIP package, 8 pins [chip_label="Horter&Kalb I2C Externder"]
  IC4 = IC, DIP package, 8 pins [chip_label="Horter&Kalb I2C Externder"]
  IC5 = IC, DIP package, 8 pins [chip_label="Horter&Kalb I2C Externder"]
  PullUp_2 = Resistor [tolerance=±5% resistance=47k package=THT]
  PullUp_3 = Resistor [tolerance=±5% resistance=47k package=THT]
  PullUp_4 = Resistor [tolerance=±5% resistance=47k package=THT]
  J2 = Camdenboss CTB0158-4 [part_number=CTB0158-4 package=THT]
  J3 = Camdenboss CTB0158-4 [part_number=CTB0158-4 package=THT]
  J4 = Camdenboss CTB0158-4 [part_number=CTB0158-4 package=THT]
  J5 = Camdenboss CTB0158-4 [part_number=CTB0158-4 package=THT]
  J6 = Camdenboss CTB0158-4 [part_number=CTB0158-4 package=THT]
  J7 = Camdenboss CTB0158-4 [part_number=CTB0158-4 package=THT]
  J8 = Camdenboss CTB0158-4 [part_number=CTB0158-4 package=THT]
  J10 = Camdenboss CTB0158-4 [part_number=CTB0158-4 package=THT]
  J11 = Camdenboss CTB0158-4 [part_number=CTB0158-4 package=THT]
  J12 = Camdenboss CTB0158-4 [part_number=CTB0158-4 package=THT]
  J13 = Camdenboss CTB0158-4 [part_number=CTB0158-4 package=THT]
  J15 = Camdenboss CTB0158-3 [part_number=CTB0158-3 package=THT]
  J20 = shrouded pin header, 16 pins [form="♂ (shrouded male)"]
  J21 = female pin header, 16 pins [form="♀ (female)"]
  J22 = female pin header, 16 pins [form="♀ (female)"]
  J23 = shrouded pin header, 16 pins [form="♂ (shrouded male)"]
  J24 = Camdenboss CTB0158-3 [part_number=CTB0158-3 package=THT]
  abhängig_von_LED_2 = Resistor [tolerance=±5% resistance=100 package=THT]
  J25 = Camdenboss CTB0158-8 [part_number=CTB0158-8 package=THT]
  J26 = Camdenboss CTB0158-8 [part_number=CTB0158-8 package=THT]
  J27 = Camdenboss CTB0158-8 [part_number=CTB0158-8 package=THT]
  J28 = Camdenboss CTB0158-8 [part_number=CTB0158-8 package=THT]

nets:
  3V3: Raspberry_Pi_3.3v3, Raspberry_Pi_3.3V3, PullUp.Pin_1, Bauteil1.VCC, Bauteil4.3.3V, IC2.pin1, IC3.pin1, PullUp_2.Pin_0, PullUp_3.Pin_0, PullUp_4.Pin_0, J15.pin3, J20.pin3, J24.pin1, J26.pin2
  N1: Raspberry_Pi_3.GPIO2, Bauteil4.SDA/SDIO, MCP1.SDA/SDI/SDO, MCP2.SDA/SDI/SDO, IC2.pin3, IC3.pin3, PullUp_2.Pin_1
  N2: Raspberry_Pi_3.GPIO3, D1.anode, PullUp_3.Pin_1
  N3: Raspberry_Pi_3.GPIO4, J15.pin1
  N4: Raspberry_Pi_3.GPIO17, PullUp.Pin_0, D1.cathode, J20.pin7
  N5: Raspberry_Pi_3.GPIO27, J20.pin14
  N6: Raspberry_Pi_3.GPIO22, R2.Pin_0, J20.pin11
  N7: Raspberry_Pi_3.GPIO5, J20.pin16
  N8: Raspberry_Pi_3.GPIO6, R5.Pin_0, J20.pin13
  N9: Raspberry_Pi_3.GPIO13, R4.Pin_0, J20.pin9
  N10: Raspberry_Pi_3.GPIO19, alle_PullDown's.Pin_0, J20.pin15
  N11: Raspberry_Pi_3.GPIO26, J20.pin2
  GND: Raspberry_Pi_3.GND, R2.Pin_1, alle_PullDown's.Pin_1, R4.Pin_1, R5.Pin_1, Bauteil1.GND, Bauteil4.GND, MCP1.GND, MCP1.ADDR2, MCP1.ADDR1, MCP2.GND, MCP2.ADDR2, MCP2.ADDR1, MCP2.ADDR0, IC3.pin2, J2.pin4, J3.pin4, J4.pin4, J5.pin4, J6.pin4, J7.pin4, J8.pin4, J15.pin2, J20.pin5, J24.pin2, J25.pin1, J26.pin1
  N12: Raspberry_Pi_3.GPIO25, J25.pin8
  N13: Raspberry_Pi_3.GPIO24, Bauteil1.CK/TX
  N14: Raspberry_Pi_3.GPIO23, Bauteil1.DO/RX
  N15: Raspberry_Pi_3.GPIO18, PullUp_4.Pin_1, J24.pin3
  VCC: Raspberry_Pi_3.5V, MCP1.VCC, MCP1.ADDR0, MCP2.VCC, J20.pin1, J25.pin2
  N16: S1.Pin_1, S1.Pin_2, J1.pin1, LED1.C, LED2.C, J23.pin5
  N17: S1.Pin_3, J23.pin7
  N18: RCWL-0516_Microwave_Radar_Motion_Sensor1.3V3, J15.terminal_3
  N19: RCWL-0516_Microwave_Radar_Motion_Sensor1.GND, J15.terminal_2
  N20: RCWL-0516_Microwave_Radar_Motion_Sensor1.OUT, J15.terminal_1
  N21: S2.Pin_1, S3.Pin_1, S3.Pin_2, S4.Pin_1, S4.Pin_2, S5.Pin_1, J23.pin3
  N22: S2.Pin_3, J23.pin11
  N23: S3.Pin_3, J23.pin15
  N24: S4.Pin_3, J23.pin9
  N25: S5.Pin_3, J23.pin13
  N26: J1.pin2, J23.pin2
  N27: LED1.A, abhängig_von_LED.Pin_0
  N28: LED2.A, abhängig_von_LED_2.Pin_0
  N29: abhängig_von_LED.Pin_1, J23.pin16
  VDD: DS1.VDD, DS2.VDD, DS3.VDD, J24.terminal_1
  N30: DS1.DQ, DS2.DQ, DS3.DQ, J24.terminal_3
  GND_2: DS1.GND, DS2.GND, DS3.GND, J24.terminal_2
  N31: Bauteil2.GND, IC4.pin2
  N32: Bauteil2.3.3V, IC4.pin1
  N33: Bauteil2.SDI/SDA, IC4.pin3
  N34: Bauteil2.SCK/SCL, IC4.pin4
  N35: Bauteil3.GND, IC5.pin2
  N36: Bauteil3.3.3V, IC5.pin1
  N37: Bauteil3.SCK/SCL, IC5.pin4
  N38: Bauteil3.SDI/SDA, IC5.pin3
  N39: Bauteil4.SCL, MCP1.SCL/SCLK, MCP2.SCL/SCLK, IC2.pin4, IC3.pin4
  N40: MCP1.GPB0, R21.Pin_0
  N41: MCP1.GPB1, R20.Pin_0
  N42: MCP1.GPB2, Alle_Vorwiderstände_abhängig_von_LEDs_2.Pin_0
  N43: MCP1.GPB3, J26.pin6
  N44: MCP1.GPB4, J26.pin5
  N45: MCP1.GPB5, J26.pin4
  N46: MCP1.GPB6, J26.pin3
  N47: MCP1.GPB7, R22.Pin_0
  N48: MCP1.GPA0, R16.Pin_0
  N49: MCP1.GPA1, R17.Pin_0
  N50: MCP1.GPA2, R18.Pin_0
  N51: MCP1.GPA3, R27.Pin_0
  N52: MCP1.GPA4, R26.Pin_0
  N53: MCP1.GPA5, R25.Pin_0
  N54: MCP1.GPA6, R24.Pin_0
  N55: MCP1.GPA7, R23.Pin_0
  N56: MCP2.GPB0, J25.pin7
  N57: MCP2.GPB1, J25.pin6
  N58: MCP2.GPB2, J25.pin5
  N59: MCP2.GPB3, J25.pin4
  N60: MCP2.GPB4, J25.pin3
  N61: MCP2.GPB7, Alle_Vorwiderstände_abhängig_von_LEDs.Pin_0
  N62: MCP2.GPA0, R7.Pin_0
  N63: MCP2.GPA1, R8.Pin_0
  N64: MCP2.GPA2, R9.Pin_0
  N65: MCP2.GPA3, R10.Pin_0
  N66: MCP2.GPA4, R11.Pin_0
  N67: MCP2.GPA5, R12.Pin_0
  N68: MCP2.GPA6, R13.Pin_0
  N69: MCP2.GPA7, R14.Pin_0
  N70: LED3.red_anode, J7.terminal_1
  N71: LED3.common_cathode, J7.terminal_4
  N72: LED3.blue_anode, J7.terminal_2
  N73: LED3.green_anode, J7.terminal_3
  N74: LED4.red_anode, J6.terminal_1
  N75: LED4.common_cathode, J6.terminal_4
  N76: LED4.blue_anode, J6.terminal_2
  N77: LED4.green_anode, J6.terminal_3
  N78: LED5.red_anode, J8.terminal_1
  N79: LED5.common_cathode, J8.terminal_4
  N80: LED5.blue_anode, J8.terminal_2
  N81: LED5.green_anode, J8.terminal_3
  N82: LED6.red_anode, J5.terminal_1
  N83: LED6.common_cathode, J5.terminal_4
  N84: LED6.blue_anode, J5.terminal_2
  N85: LED6.green_anode, J5.terminal_3
  N86: LED7.red_anode, J4.terminal_1
  N87: LED7.common_cathode, J4.terminal_4
  N88: LED7.blue_anode, J4.terminal_2
  N89: LED7.green_anode, J4.terminal_3
  N90: LED8.red_anode, J3.terminal_1
  N91: LED8.common_cathode, J3.terminal_4
  N92: LED8.blue_anode, J3.terminal_2
  N93: LED8.green_anode, J3.terminal_3
  N94: LED9.red_anode, J2.terminal_1
  N95: LED9.common_cathode, J2.terminal_4
  N96: LED9.blue_anode, J2.terminal_2
  N97: LED9.green_anode, J2.terminal_3
  N98: R7.Pin_1, J7.pin3
  N99: R8.Pin_1, J7.pin2
  N100: R9.Pin_1, J7.pin1
  N101: R10.Pin_1, J6.pin3
  N102: R11.Pin_1, J6.pin2
  N103: R12.Pin_1, J6.pin1
  N104: R13.Pin_1, J8.pin3
  N105: R14.Pin_1, J8.pin2
  N106: Alle_Vorwiderstände_abhängig_von_LEDs.Pin_1, J8.pin1
  N107: R16.Pin_1, J5.pin3
  N108: R17.Pin_1, J5.pin2
  N109: R18.Pin_1, J5.pin1
  N110: Alle_Vorwiderstände_abhängig_von_LEDs_2.Pin_1, J2.pin1
  N111: R20.Pin_1, J2.pin2
  N112: R21.Pin_1, J2.pin3
  N113: R22.Pin_1, J3.pin1
  N114: R23.Pin_1, J3.pin2
  N115: R24.Pin_1, J3.pin3
  N116: R25.Pin_1, J4.pin1
  N117: R26.Pin_1, J4.pin2
  N118: R27.Pin_1, J4.pin3
  N119: IC2.pin5, J11.pin4
  N120: IC2.pin6, J11.pin3
  N121: IC2.pin7, J11.pin2
  N122: IC2.pin8, J11.pin1
  N123: IC3.pin5, J10.pin4
  N124: IC3.pin6, J10.pin3
  N125: IC3.pin7, J10.pin2
  N126: IC3.pin8, J10.pin1
  N127: IC4.pin5, J12.pin1
  N128: IC4.pin6, J12.pin2
  N129: IC4.pin7, J12.pin3
  N130: IC4.pin8, J12.pin4
  N131: IC5.pin5, J13.pin1
  N132: IC5.pin6, J13.pin2
  N133: IC5.pin7, J13.pin3
  N134: IC5.pin8, J13.pin4
  N135: J10.terminal_1, J13.terminal_4
  N136: J10.terminal_2, J13.terminal_3
  N137: J10.terminal_3, J13.terminal_2
  N138: J10.terminal_4, J13.terminal_1
  N139: J11.terminal_1, J12.terminal_4
  N140: J11.terminal_2, J12.terminal_3
  N141: J11.terminal_3, J12.terminal_2
  N142: J11.terminal_4, J12.terminal_1
  N143: J21.pin1, J22.pin1
  N144: J21.pin2, J22.pin2
  N145: J21.pin3, J22.pin3
  N146: J21.pin4, J22.pin4
  N147: J21.pin5, J22.pin5
  N148: J21.pin6, J22.pin6
  N149: J21.pin7, J22.pin7
  N150: J21.pin8, J22.pin8
  N151: J21.pin9, J22.pin9
  N152: J21.pin10, J22.pin10
  N153: J21.pin11, J22.pin11
  N154: J21.pin12, J22.pin12
  N155: J21.pin13, J22.pin13
  N156: J21.pin14, J22.pin14
  N157: J21.pin15, J22.pin15
  N158: J21.pin16, J22.pin16
  N159: J23.pin14, abhängig_von_LED_2.Pin_1
  N160: J25.terminal_1, J27.terminal_8
  N161: J25.terminal_2, J27.terminal_7
  N162: J25.terminal_3, J27.terminal_6
  N163: J25.terminal_4, J27.terminal_5
  N164: J25.terminal_5, J27.terminal_4
  N165: J25.terminal_6, J27.terminal_3
  N166: J25.terminal_7, J27.terminal_2
  N167: J25.terminal_8, J27.terminal_1
  N168: J26.terminal_1, J28.terminal_8
  N169: J26.terminal_2, J28.terminal_7
  N170: J26.terminal_3, J28.terminal_6
  N171: J26.terminal_4, J28.terminal_5
  N172: J26.terminal_5, J28.terminal_4
  N173: J26.terminal_6, J28.terminal_3

notes:
  Lage Live
  Kalibr. Gaswaage
  Querlage ok
  Buzzer
  Kalibr. Lage
  Temperatursensoren Kühlschrank
  Klimasensoren
  ACHTUNG:
  Über P82B715 an zwei langen Leitungen
  Lagesensor
  GPIO Port Expander 1
  GPIO Port Expander 2
  LEDs am Caravan
  Frischwassertank
  Füllstands-Anzeige
  separate Platine
  (siehe separaten
  Schaltplan)
  verbunden über CAT7 Kabel
  Ein-/Aus- Taster
  LED pinorder:
  grün, rot, blau !!
  grün in dieser Abbildung also oben
  Flachband zum Deckel
  CaravanPi, Bauteile im Rechteck = auf Platine. Rest über Kabel und Klemmfelder verbunden
  LED Bewegung
  Fäkalientank-Füllstands-Anzeige
  separate Platine
  (siehe separaten Schaltplan)
  verbunden über CAT7 Kabel
  GND
  3,3 V
  5 V (StromPi 3A)
  Wäge-
  sensor

custom parts:
  RCWL-0516 Microwave Radar Motion Sensor Module: The RCWL-0516 is a microwave radar motion sensor module. Input voltage is 4V to 28V. The 3V3 pin is a power output.
  Adafruit ADXL345: Filling out our accelerometer offerings, we now have the really lovely digital ADXL345 from Analog Devices, a triple-axis accelerometer with digital I2C and SPI interface breakout. We added an on-board 3.3V regulator and logic-level shifting circuitry, making it a perfect choice for interfacing with any 3V or 5V microcontroller such as the Arduino. The sensor has three axes of measurements, X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
  CJMCU2317-MCP23017: The MCP23017 device family provides 16-bit, general purpose parallel I/O expansion for I2C bus. The MCP23X17 consists of multiple 8-bit configuration registers for input, output and polarity selection. The system master can enable the I/Os as either inputs or outputs by writing the I/O configuration bits (IODIRA/B). The data for each input or output is kept in the corresponding input or output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
