# Fritzing sketch Frischwassertank-V2 (saved by Fritzing 0.9.4)
circuit board: 13.8517cm x 7.35784cm
breadboards: 1

parts:
  IC1 = ULN2003A [package="SO16 [SMD]"]
  R5 = Resistor [tolerance=±5% resistance=10k package=THT]
  R7 = Resistor [tolerance=±5% resistance=10k package=THT]
  R8 = Resistor [tolerance=±5% resistance=10k package=THT]
  am_CaravanPi = CJMCU2317-MCP23017
  alle_PullUps = Resistor [tolerance=±5% resistance=47k package=THT]
  Wasserhähne_Toilettenspülung = Pushbutton [package=THT]
  Pumpe_im_Frischwassertank = DC Motor
  Taster_an_Anzeige = Pushbutton [package=THT]
  Freilaufdiode = Diode [part_number=1N4003 package=diode-1n4001]
  Füllstandssonde_im_Tank = mystery part, 5 pins [chip_label="Schaudt Sonde"]
  Füllstandsanzeige_original_mit_Taster = mystery part, 7 pins [chip_label="Schaudt LT410"]
  R10 = Resistor [tolerance=±5% resistance=1k package=THT]
  Schutz_vor_Originaltaster_(Fremdspeisung) = Diode [part_number=1N4003 package=diode-1n4001]
  Relais_5V_KY-019 = KY-019 5V Relay Module [package="Breakout board"]
  R6 = Resistor [tolerance=±5% resistance=10k package=THT]
  Raspberry_Pi_1 = Raspberry Pi 3 [part_number=RPI-3-V1.2]
  J1 = Camdenboss CTB0158-8 [part_number=CTB0158-8 package=THT]
  J2 = Camdenboss CTB0158-8 [part_number=CTB0158-8 package=THT]
  J3 = Camdenboss CTB0158-5 [part_number=CTB0158-5 package=THT]
  J4 = Camdenboss CTB0158-2 [part_number=CTB0158-2 package=THT]
  J5 = Camdenboss CTB0158-5 [part_number=CTB0158-5 package=THT]

nets:
  N1: IC1.In_1, J3.pin4, J5.pin4
  N2: IC1.In_2, J3.pin3, J5.pin3
  N3: IC1.In_3, J3.pin2, J5.pin2
  N4: IC1.In_4, J3.pin1, J5.pin1
  N5: IC1.In_5, Freilaufdiode.C, R10.Pin_0
  N6: IC1.0V, Freilaufdiode.A, Relais_5V_KY-019.-, J2.pin1, J4.pin2
  N7: IC1.COM_-_Common, R5.Pin_0, R7.Pin_0, R8.Pin_0, alle_PullUps.Pin_0, Relais_5V_KY-019.+, Relais_5V_KY-019.Common, R6.Pin_0, J2.pin2
  N8: IC1.Out_5, R7.Pin_1, J2.pin8
  N9: IC1.Out_4, R8.Pin_1, J2.pin4
  N10: IC1.Out_3, R5.Pin_1, J2.pin5
  N11: IC1.Out_2, R6.Pin_1, J2.pin6
  N12: IC1.Out_1, alle_PullUps.Pin_1, J2.pin7
  GND: am_CaravanPi.GND, Raspberry_Pi_1.GND, J1.pin1
  VCC: am_CaravanPi.VCC, Raspberry_Pi_1.5V, J1.pin2
  N13: am_CaravanPi.GPB0, J1.pin7
  N14: am_CaravanPi.GPB1, J1.pin6
  N15: am_CaravanPi.GPB2, J1.pin5
  N16: am_CaravanPi.GPB3, J1.pin4
  N17: am_CaravanPi.GPB4, J1.pin3
  N18: Wasserhähne_Toilettenspülung.leg0, Pumpe_im_Frischwassertank.pin_1, J4.terminal_1
  12V: Wasserhähne_Toilettenspülung.leg1, Füllstandsanzeige_original_mit_Taster.pin6
  GND_2: Pumpe_im_Frischwassertank.pin_2, Füllstandsanzeige_original_mit_Taster.pin7, J4.terminal_2
  N19: Taster_an_Anzeige.leg0, Füllstandsanzeige_original_mit_Taster.pin5
  N20: Taster_an_Anzeige.leg1, J5.terminal_5
  N21: Füllstandssonde_im_Tank.pin1, J3.terminal_4
  N22: Füllstandssonde_im_Tank.pin2, J3.terminal_3
  N23: Füllstandssonde_im_Tank.pin3, J3.terminal_2
  N24: Füllstandssonde_im_Tank.pin4, J3.terminal_1
  N25: Füllstandssonde_im_Tank.pin5, J3.terminal_5
  N26: Füllstandsanzeige_original_mit_Taster.pin1, J5.terminal_4
  N27: Füllstandsanzeige_original_mit_Taster.pin2, J5.terminal_3
  N28: Füllstandsanzeige_original_mit_Taster.pin3, J5.terminal_2
  N29: Füllstandsanzeige_original_mit_Taster.pin4, J5.terminal_1
  N30: R10.Pin_1, J4.pin1
  N31: Schutz_vor_Originaltaster_(Fremdspeisung).A, Relais_5V_KY-019.NO
  N32: Schutz_vor_Originaltaster_(Fremdspeisung).C, J3.pin5, J5.pin5
  N33: Relais_5V_KY-019.S, J2.pin3
  N34: Raspberry_Pi_1.GPIO25, J1.pin8
  N35: J1.terminal_1, J2.terminal_1
  N36: J1.terminal_2, J2.terminal_2
  N37: J1.terminal_3, J2.terminal_3
  N38: J1.terminal_4, J2.terminal_4
  N39: J1.terminal_5, J2.terminal_5
  N40: J1.terminal_6, J2.terminal_6
  N41: J1.terminal_7, J2.terminal_7
  N42: J1.terminal_8, J2.terminal_8

notes:
  Caravan 12 V Netz
  CaravanPi 5V
  Cat7 Kabel
  Caravan GND und CaravanPi GND
  werden verbunden;
  sollten über den StromPi ohnehin identisch sein
  Sondenkabel am Tank auftrennen und auf Platine beidseits einklemmen

custom parts:
  CJMCU2317-MCP23017: The MCP23017 device family provides 16-bit, general purpose parallel I/O expansion for I2C bus. The MCP23X17 consists of multiple 8-bit configuration registers for input, output and polarity selection. The system master can enable the I/Os as either inputs or outputs by writing the I/O configuration bits (IODIRA/B). The data for each input or output is kept in the corresponding input or output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
  KY-019 5V Relay Module: KY-019 5V Relay module, used to control AC circuits.
