# Fritzing sketch Fäkalientank (saved by Fritzing 0.9.4)
breadboards: 1

parts:
  am_CaravanPi = CJMCU2317-MCP23017
  Raspberry_Pi_1 = Raspberry Pi 3 [part_number=RPI-3-V1.2]
  J1 = Camdenboss CTB0158-8 [part_number=CTB0158-8 package=THT]
  J2 = Camdenboss CTB0158-8 [part_number=CTB0158-8 package=THT]
  alle_PullDowns = Resistor [tolerance=±5% resistance=47k package=THT]
  alle_PullDowns_2 = Resistor [tolerance=±5% resistance=47k package=THT]
  alle_PullDowns_2 = Resistor [tolerance=±5% resistance=47k package=THT]
  alle_PullDowns_3 = Resistor [tolerance=±5% resistance=47k package=THT]
  zusätzliche_Reed-Kontakte_am_Fäkalientank = Reed switch [package=THT]
  S2 = Reed switch [package=THT]
  S3 = Reed switch [package=THT]
  S4 = Reed switch [package=THT]

nets:
  GND: am_CaravanPi.GND, Raspberry_Pi_1.GND, J1.pin1
  VCC: am_CaravanPi.VCC, Raspberry_Pi_1.5V, J1.pin2
  N1: am_CaravanPi.GPB3, J1.pin6
  N2: am_CaravanPi.GPB4, J1.pin5
  N3: am_CaravanPi.GPB5, J1.pin4
  N4: am_CaravanPi.GPB6, J1.pin3
  N5: J1.terminal_1, J2.terminal_1
  N6: J1.terminal_2, J2.terminal_2
  N7: J1.terminal_3, J2.terminal_3
  N8: J1.terminal_4, J2.terminal_4
  N9: J1.terminal_5, J2.terminal_5
  N10: J1.terminal_6, J2.terminal_6
  N11: J1.terminal_7, J2.terminal_7
  N12: J1.terminal_8, J2.terminal_8
  N13: J2.pin1, alle_PullDowns.Pin_1, alle_PullDowns_2.Pin_1, alle_PullDowns_3.Pin_1
  N14: J2.pin2, zusätzliche_Reed-Kontakte_am_Fäkalientank.pin_1, S2.pin_1, S3.pin_1, S4.pin_1
  N15: J2.pin3, alle_PullDowns_2.Pin_0, zusätzliche_Reed-Kontakte_am_Fäkalientank.pin_2
  N16: J2.pin4, alle_PullDowns_2.Pin_0, S2.pin_2
  N17: J2.pin5, alle_PullDowns_3.Pin_0, S3.pin_2
  N18: J2.pin6, alle_PullDowns.Pin_0, S4.pin_2

notes:
  Cat7 Kabel

custom parts:
  CJMCU2317-MCP23017: The MCP23017 device family provides 16-bit, general purpose parallel I/O expansion for I2C bus. The MCP23X17 consists of multiple 8-bit configuration registers for input, output and polarity selection. The system master can enable the I/Os as either inputs or outputs by writing the I/O configuration bits (IODIRA/B). The data for each input or output is kept in the corresponding input or output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
